// Logisim project processor-design.circ as structural Verilog: 5 circuits, main circuit register_file
// Register File
module register_file (
  input  Clock,
  input  RegWEn,
  input  [31:0] dataW,
  input  [4:0] rsR2,
  input  [4:0] rsW,
  input  [4:0] rsR1,
  output [31:0] data_R2,
  output [31:0] data_R1
);

  wire demultiplexer_1_out1, demultiplexer_1_out2, demultiplexer_1_out3, demultiplexer_1_out4,
       demultiplexer_1_out5, demultiplexer_1_out6, demultiplexer_1_out7, demultiplexer_1_out8,
       demultiplexer_1_out9, demultiplexer_1_out10, demultiplexer_1_out11, demultiplexer_1_out12,
       demultiplexer_1_out13, demultiplexer_1_out14, demultiplexer_1_out15, demultiplexer_1_out16,
       demultiplexer_1_out17, demultiplexer_1_out18, demultiplexer_1_out19, demultiplexer_1_out20,
       demultiplexer_1_out21, demultiplexer_1_out22, demultiplexer_1_out23, demultiplexer_1_out24,
       demultiplexer_1_out25, demultiplexer_1_out26, demultiplexer_1_out27, demultiplexer_1_out28,
       demultiplexer_1_out29, demultiplexer_1_out30, demultiplexer_1_out31;
  wire [31:0] register_1_q, register_2_q, register_3_q, register_4_q, register_5_q, register_6_q,
       register_7_q, register_8_q, register_9_q, register_10_q, register_11_q, register_12_q, register_13_q,
       register_14_q, register_15_q, register_16_q, register_17_q, register_18_q, register_19_q,
       register_20_q, register_21_q, register_22_q, register_23_q, register_24_q, register_25_q,
       register_26_q, register_27_q, register_28_q, register_29_q, register_30_q, register_31_q,
       register_32_q;

  Demultiplexer #(.select(5), .enable("false")) demultiplexer_1 (
    .out1(demultiplexer_1_out1), .out2(demultiplexer_1_out2), .out3(demultiplexer_1_out3),
    .out4(demultiplexer_1_out4), .out5(demultiplexer_1_out5), .out6(demultiplexer_1_out6),
    .out7(demultiplexer_1_out7), .out8(demultiplexer_1_out8), .out9(demultiplexer_1_out9),
    .out10(demultiplexer_1_out10), .out11(demultiplexer_1_out11), .out12(demultiplexer_1_out12),
    .out13(demultiplexer_1_out13), .out14(demultiplexer_1_out14), .out15(demultiplexer_1_out15),
    .out16(demultiplexer_1_out16), .out17(demultiplexer_1_out17), .out18(demultiplexer_1_out18),
    .out19(demultiplexer_1_out19), .out20(demultiplexer_1_out20), .out21(demultiplexer_1_out21),
    .out22(demultiplexer_1_out22), .out23(demultiplexer_1_out23), .out24(demultiplexer_1_out24),
    .out25(demultiplexer_1_out25), .out26(demultiplexer_1_out26), .out27(demultiplexer_1_out27),
    .out28(demultiplexer_1_out28), .out29(demultiplexer_1_out29), .out30(demultiplexer_1_out30),
    .out31(demultiplexer_1_out31), .in(RegWEn), .sel(rsW));  // open: out0
  Register #(.width(32), .Select("low")) register_1 (
    .D(dataW), .en(demultiplexer_1_out7), .Q(register_1_q), .clk(Clock));  // open: clr
  Register #(.width(32), .Select("low")) register_2 (
    .D(dataW), .en(demultiplexer_1_out15), .Q(register_2_q), .clk(Clock));  // open: clr
  Register #(.width(32), .Select("low")) register_3 (
    .D(dataW), .en(demultiplexer_1_out23), .Q(register_3_q), .clk(Clock));  // open: clr
  Register #(.width(32), .Select("low")) register_4 (
    .D(dataW), .en(demultiplexer_1_out31), .Q(register_4_q), .clk(Clock));  // open: clr
  Register #(.width(32), .Select("low")) register_5 (
    .D(dataW), .en(demultiplexer_1_out6), .Q(register_5_q), .clk(Clock));  // open: clr
  Register #(.width(32), .Select("low")) register_6 (
    .D(dataW), .en(demultiplexer_1_out14), .Q(register_6_q), .clk(Clock));  // open: clr
  Register #(.width(32), .Select("low")) register_7 (
    .D(dataW), .en(demultiplexer_1_out22), .Q(register_7_q), .clk(Clock));  // open: clr
  Register #(.width(32), .Select("low")) register_8 (
    .D(dataW), .en(demultiplexer_1_out30), .Q(register_8_q), .clk(Clock));  // open: clr
  Register #(.width(32), .Select("low")) register_9 (
    .D(dataW), .en(demultiplexer_1_out29), .Q(register_9_q), .clk(Clock));  // open: clr
  Register #(.width(32), .Select("low")) register_10 (
    .D(dataW), .en(demultiplexer_1_out5), .Q(register_10_q), .clk(Clock));  // open: clr
  Register #(.width(32), .Select("low")) register_11 (
    .D(dataW), .en(demultiplexer_1_out13), .Q(register_11_q), .clk(Clock));  // open: clr
  Register #(.width(32), .Select("low")) register_12 (
    .D(dataW), .en(demultiplexer_1_out20), .Q(register_12_q), .clk(Clock));  // open: clr
  Register #(.width(32), .Select("low")) register_13 (
    .D(dataW), .en(demultiplexer_1_out21), .Q(register_13_q), .clk(Clock));  // open: clr
  Register #(.width(32), .Select("low")) register_14 (
    .D(dataW), .en(demultiplexer_1_out28), .Q(register_14_q), .clk(Clock));  // open: clr
  Register #(.width(32), .Select("low")) register_15 (
    .D(dataW), .en(demultiplexer_1_out3), .Q(register_15_q), .clk(Clock));  // open: clr
  Register #(.width(32), .Select("low")) register_16 (
    .D(dataW), .en(demultiplexer_1_out4), .Q(register_16_q), .clk(Clock));  // open: clr
  Register #(.width(32), .Select("low")) register_17 (
    .D(dataW), .en(demultiplexer_1_out11), .Q(register_17_q), .clk(Clock));  // open: clr
  Register #(.width(32), .Select("low")) register_18 (
    .D(dataW), .en(demultiplexer_1_out12), .Q(register_18_q), .clk(Clock));  // open: clr
  Register #(.width(32), .Select("low")) register_19 (
    .D(dataW), .en(demultiplexer_1_out19), .Q(register_19_q), .clk(Clock));  // open: clr
  Register #(.width(32), .Select("low")) register_20 (
    .D(dataW), .en(demultiplexer_1_out27), .Q(register_20_q), .clk(Clock));  // open: clr
  Register #(.width(32), .Select("low")) register_21 (
    .D(dataW), .en(demultiplexer_1_out2), .Q(register_21_q), .clk(Clock));  // open: clr
  Register #(.width(32), .Select("low")) register_22 (
    .D(dataW), .en(demultiplexer_1_out10), .Q(register_22_q), .clk(Clock));  // open: clr
  Register #(.width(32), .Select("low")) register_23 (
    .D(dataW), .en(demultiplexer_1_out18), .Q(register_23_q), .clk(Clock));  // open: clr
  Register #(.width(32), .Select("low")) register_24 (
    .D(dataW), .en(demultiplexer_1_out26), .Q(register_24_q), .clk(Clock));  // open: clr
  Register #(.width(32), .Select("low")) register_25 (
    .D(dataW), .en(demultiplexer_1_out25), .Q(register_25_q), .clk(Clock));  // open: clr
  Register #(.width(32), .Select("low")) register_26 (
    .D(dataW), .en(demultiplexer_1_out1), .Q(register_26_q), .clk(Clock));  // open: clr
  Register #(.width(32), .Select("low")) register_27 (
    .D(dataW), .en(demultiplexer_1_out9), .Q(register_27_q), .clk(Clock));  // open: clr
  Register #(.width(32), .Select("low")) register_28 (
    .D(dataW), .en(demultiplexer_1_out16), .Q(register_28_q), .clk(Clock));  // open: clr
  Register #(.width(32), .Select("low")) register_29 (
    .D(dataW), .en(demultiplexer_1_out17), .Q(register_29_q), .clk(Clock));  // open: clr
  Register #(.width(32), .Select("low")) register_30 (
    .D(dataW), .en(demultiplexer_1_out24), .Q(register_30_q), .clk(Clock));  // open: clr
  Register #(.width(32), .Select("low")) register_31 (
    .D({32{1'b0}}), .en(1'b1), .Q(register_31_q), .clk(Clock));  // open: clr
  Register #(.width(32), .Select("low")) register_32 (
    .D(dataW), .en(demultiplexer_1_out8), .Q(register_32_q), .clk(Clock));  // open: clr
  Multiplexer #(.select(5), .width(32), .enable("false")) multiplexer_1 (
    .in0(register_31_q), .in1(register_26_q), .in2(register_21_q), .in3(register_15_q), .in4(register_16_q),
    .in5(register_10_q), .in6(register_5_q), .in7(register_1_q), .in8(register_32_q), .in9(register_27_q),
    .in10(register_22_q), .in11(register_17_q), .in12(register_18_q), .in13(register_11_q),
    .in14(register_6_q), .in15(register_2_q), .in16(register_28_q), .in17(register_29_q),
    .in18(register_23_q), .in19(register_19_q), .in20(register_12_q), .in21(register_13_q),
    .in22(register_7_q), .in23(register_3_q), .in24(register_30_q), .in25(register_25_q),
    .in26(register_24_q), .in27(register_20_q), .in28(register_14_q), .in29(register_9_q),
    .in30(register_8_q), .in31(register_4_q), .out(data_R2), .sel(rsR2));
  Multiplexer #(.select(5), .width(32), .enable("false")) multiplexer_2 (
    .in0(register_31_q), .in1(register_26_q), .in2(register_21_q), .in3(register_15_q), .in4(register_16_q),
    .in5(register_10_q), .in6(register_5_q), .in7(register_1_q), .in8(register_32_q), .in9(register_27_q),
    .in10(register_22_q), .in11(register_17_q), .in12(register_18_q), .in13(register_11_q),
    .in14(register_6_q), .in15(register_2_q), .in16(register_28_q), .in17(register_29_q),
    .in18(register_23_q), .in19(register_19_q), .in20(register_12_q), .in21(register_13_q),
    .in22(register_7_q), .in23(register_3_q), .in24(register_30_q), .in25(register_25_q),
    .in26(register_24_q), .in27(register_20_q), .in28(register_14_q), .in29(register_9_q),
    .in30(register_8_q), .in31(register_4_q), .out(data_R1), .sel(rsR1));

  // Notes on the sheet:
  //   REGISTER FILE (CONTAINS 32x32-bit REGISTERS IN RV32I)
endmodule

// Instruction Decoder
module instruction_decoder (
  input  [31:0] in_1,
  output [11:0] imm__i_format,
  output [4:0] rd,
  output [2:0] func3,
  output [4:0] rs1,
  output [4:0] rs2,
  output [6:0] func7,
  output [12:0] immediate__branch_format,
  output [11:0] immediate__store_format
);


  assign func3 = in_1[14:12];
  assign func7 = in_1[31:25];
  assign imm__i_format = in_1[31:20];
  assign immediate__branch_format = {in_1[31], in_1[7], in_1[30:25], in_1[11:8], 1'b0};
  assign immediate__store_format = {in_1[31:25], in_1[11:7]};
  assign rd = in_1[11:7];
  assign rs1 = in_1[19:15];
  assign rs2 = in_1[24:20];

  // Notes on the sheet:
  //   decoding store instructions
endmodule

// ALU
module arithmetic_logic_unit (
  input  [6:0] func7,
  input  [31:0] rs1,
  input  [31:0] rs2_imm_i,
  input  [12:0] imm_branch,
  input  [11:0] immediate_store,
  input  [2:0] func3,
  output [31:0] Output_R_I,
  output [23:0] Output_branchJumpAdd,
  output Output_Branch,
  output [23:0] Output_StoreAddress,
  output [31:0] Output_StoreData,
  output [23:0] Output_LoadAddress
);

  wire comparator_1_lt, comparator_2_lt, comparator_3_eq, comparator_3_gt, comparator_3_lt, comparator_4_eq,
       comparator_4_gt, comparator_4_lt, not_1_out, or_2_out, or_3_out;
  wire [23:0] bit_extender_4_out;
  wire [31:0] adder_1_out, adder_2_out, adder_3_out, and_1_out, bit_extender_1_out, bit_extender_2_out,
       bit_extender_3_out, bit_extender_5_out, bit_extender_6_out, multiplexer_2_out, multiplexer_4_out,
       or_1_out, shifter_1_out, shifter_2_out, shifter_3_out, subtractor_1_out, xor_1_out;

  assign bit_extender_1_out = {{20{1'b0}}, immediate_store};  // Bit_Extender bit_extender_1
  assign bit_extender_2_out = {{24{1'b0}}, rs2_imm_i[7:0]};  // Bit_Extender bit_extender_2
  assign bit_extender_3_out = {{16{1'b0}}, rs2_imm_i[15:0]};  // Bit_Extender bit_extender_3
  Adder #(.width(32)) adder_1 (.a(bit_extender_1_out), .b(rs1), .out(adder_1_out));  // open: cin, cout
  Multiplexer #(.select(3), .width(32), .enable("false")) multiplexer_1 (
    .in0(bit_extender_2_out), .in1(bit_extender_3_out), .in2(rs2_imm_i), .out(Output_StoreData), .sel(func3));  // open: in3, in4, in5, in6, in7
  Adder #(.width(32)) adder_2 (.a(rs2_imm_i), .b(rs1), .out(adder_2_out));  // open: cin, cout
  Adder #(.width(32)) adder_3 (.a(rs1), .b(rs2_imm_i), .out(adder_3_out));  // open: cin, cout
  assign and_1_out = rs1 & rs2_imm_i;  // AND_Gate and_1, 32 bits wide
  assign or_1_out = rs1 | rs2_imm_i;  // OR_Gate or_1, 32 bits wide
  assign xor_1_out = rs1 ^ rs2_imm_i;  // XOR_Gate xor_1, 32 bits wide
  Shifter #(.width(32)) shifter_1 (.in(rs1), .\dist (rs2_imm_i[4:0]), .out(shifter_1_out));
  Shifter #(.width(32), .shift("lr")) shifter_2 (.in(rs1), .\dist (rs2_imm_i[4:0]), .out(shifter_2_out));
  Shifter #(.width(32), .shift("ar")) shifter_3 (.in(rs1), .\dist (rs2_imm_i[4:0]), .out(shifter_3_out));
  Comparator #(.width(32)) comparator_1 (.a(rs1), .b(rs2_imm_i), .lt(comparator_1_lt));  // open: gt, eq
  Comparator #(.width(32), .mode("unsigned")) comparator_2 (
    .a(rs1), .b(rs2_imm_i), .lt(comparator_2_lt));  // open: gt, eq
  assign bit_extender_4_out = {{11{1'b0}}, imm_branch};  // Bit_Extender bit_extender_4
  Comparator #(.width(32)) comparator_3 (
    .a(rs1), .b(rs2_imm_i), .gt(comparator_3_gt), .eq(comparator_3_eq), .lt(comparator_3_lt));
  Comparator #(.width(32), .mode("unsigned")) comparator_4 (
    .a(rs1), .b(rs2_imm_i), .gt(comparator_4_gt), .eq(comparator_4_eq), .lt(comparator_4_lt));
  Subtractor #(.width(32)) subtractor_1 (.a(rs1), .b(rs2_imm_i), .out(subtractor_1_out));  // open: bin, bout
  assign bit_extender_5_out = {{31{1'b0}}, comparator_1_lt};  // Bit_Extender bit_extender_5
  assign bit_extender_6_out = {{31{1'b0}}, comparator_2_lt};  // Bit_Extender bit_extender_6
  or or_2 (or_2_out, comparator_3_gt, comparator_3_eq);
  or or_3 (or_3_out, comparator_4_gt, comparator_4_eq);
  Multiplexer #(.width(32), .enable("false")) multiplexer_2 (
    .in0(shifter_2_out), .in1(shifter_3_out), .out(multiplexer_2_out), .sel(func7[5]));
  Divider #(.width(24)) divider_1 (.a(bit_extender_4_out), .b(24'h4), .out(Output_branchJumpAdd));  // open: upper, rem
  not not_1 (not_1_out, comparator_3_eq);
  Multiplexer #(.select(3), .enable("false")) multiplexer_3 (
    .in0(comparator_3_eq), .in1(not_1_out), .in4(comparator_3_lt), .in5(or_2_out), .in6(comparator_4_lt),
    .in7(or_3_out), .out(Output_Branch), .sel(func3));  // open: in2, in3
  Bit_Extender #(.in_width(32), .out_width(24), .\type ("zero")) bit_extender_7 (
    .in(adder_1_out), .out(Output_StoreAddress));
  Bit_Extender #(.in_width(32), .out_width(24), .\type ("zero")) bit_extender_8 (
    .in(adder_2_out), .out(Output_LoadAddress));
  Multiplexer #(.width(32), .enable("false")) multiplexer_4 (
    .in0(adder_3_out), .in1(subtractor_1_out), .out(multiplexer_4_out), .sel(func7[5]));
  Multiplexer #(.select(3), .width(32), .enable("false")) multiplexer_5 (
    .in0(multiplexer_4_out), .in1(shifter_1_out), .in2(bit_extender_5_out), .in3(bit_extender_6_out),
    .in4(xor_1_out), .in5(multiplexer_2_out), .in6(or_1_out), .in7(and_1_out), .out(Output_R_I), .sel(func3));

  // Notes on the sheet:
  //   Data rs2
  //   store immediate
  //   Data rs1
  //   ALU FOR R AND I TYPE INSTRUCTIONS
  //   ALU FOR B TYPE INSTRUCTIONS
  //   memory address to store
  //   value to store
  //   ALU FOR S TYPE INSTRUCTIONS
  //   func3
endmodule

// DataPath
module data_path (
);

  wire arithmetic_logic_unit_1_output_branch, clock_1_out, control_unit_1_branchinstruction,
       control_unit_1_bsel, control_unit_1_dmemen, control_unit_1_dmemselectforload, control_unit_1_regwen;
  wire [2:0] instruction_decoder_1_func3;
  wire [4:0] instruction_decoder_1_rd, instruction_decoder_1_rs1, instruction_decoder_1_rs2;
  wire [6:0] instruction_decoder_1_func7;
  wire [11:0] instruction_decoder_1_imm__i_format, instruction_decoder_1_immediate__store_format;
  wire [12:0] instruction_decoder_1_immediate__branch_format;
  wire [23:0] adder_1_out, arithmetic_logic_unit_1_output_branchjumpadd,
       arithmetic_logic_unit_1_output_loadaddress, arithmetic_logic_unit_1_output_storeaddress,
       multiplexer_1_out, multiplexer_2_out, multiplexer_5_out, register_1_q;
  wire [31:0] arithmetic_logic_unit_1_output_r_i, arithmetic_logic_unit_1_output_storedata,
       bit_extender_1_out, multiplexer_3_out, multiplexer_4_out, ram_1_data, register_file_1_data_r1,
       register_file_1_data_r2, rom_1_data;

  Multiplexer #(.width(24), .enable("false")) multiplexer_1 (
    .in0(24'h1), .in1(arithmetic_logic_unit_1_output_branchjumpadd), .out(multiplexer_1_out),
    .sel(arithmetic_logic_unit_1_output_branch));
  Clock clock_1 (.out(clock_1_out));
  Multiplexer #(.width(24), .enable("false")) multiplexer_2 (
    .in0(24'h1), .in1(multiplexer_1_out), .out(multiplexer_2_out), .sel(control_unit_1_branchinstruction));
  Register #(.width(24), .Select("low")) register_1 (
    .D(adder_1_out), .Q(register_1_q), .clk(clock_1_out));  // open: en, clr
  Adder #(.width(24)) adder_1 (.a(register_1_q), .b(multiplexer_2_out), .out(adder_1_out));  // open: cin, cout
  ROM #(.addrWidth(24), .dataWidth(32), .Select("low")) rom_1 (.addr(register_1_q), .data(rom_1_data));
  instruction_decoder instruction_decoder_1 (
    .in_1(rom_1_data), .imm__i_format(instruction_decoder_1_imm__i_format), .rd(instruction_decoder_1_rd),
    .func3(instruction_decoder_1_func3), .rs1(instruction_decoder_1_rs1), .rs2(instruction_decoder_1_rs2),
    .func7(instruction_decoder_1_func7),
    .immediate__branch_format(instruction_decoder_1_immediate__branch_format),
    .immediate__store_format(instruction_decoder_1_immediate__store_format));
  control_unit control_unit_1 (
    .in_1(rom_1_data), .RegWEn(control_unit_1_regwen), .Bsel(control_unit_1_bsel),
    .DMemEn(control_unit_1_dmemen), .branchInstruction(control_unit_1_branchinstruction),
    .DMemSelectForLoad(control_unit_1_dmemselectforload));
  Multiplexer #(.width(32), .enable("false")) multiplexer_3 (
    .in0(arithmetic_logic_unit_1_output_r_i), .in1(ram_1_data), .out(multiplexer_3_out),
    .sel(control_unit_1_dmemselectforload));
  register_file register_file_1 (
    .Clock(clock_1_out), .RegWEn(control_unit_1_regwen), .dataW(multiplexer_3_out),
    .rsR2(instruction_decoder_1_rs2), .rsW(instruction_decoder_1_rd), .rsR1(instruction_decoder_1_rs1),
    .data_R2(register_file_1_data_r2), .data_R1(register_file_1_data_r1));
  assign bit_extender_1_out = {{20{1'b0}}, instruction_decoder_1_imm__i_format};  // Bit_Extender bit_extender_1
  Multiplexer #(.width(32), .enable("false")) multiplexer_4 (
    .in0(register_file_1_data_r2), .in1(bit_extender_1_out), .out(multiplexer_4_out),
    .sel(control_unit_1_bsel));
  arithmetic_logic_unit arithmetic_logic_unit_1 (
    .func7(instruction_decoder_1_func7), .rs1(register_file_1_data_r1), .rs2_imm_i(multiplexer_4_out),
    .imm_branch(instruction_decoder_1_immediate__branch_format),
    .immediate_store(instruction_decoder_1_immediate__store_format), .func3(instruction_decoder_1_func3),
    .Output_R_I(arithmetic_logic_unit_1_output_r_i),
    .Output_branchJumpAdd(arithmetic_logic_unit_1_output_branchjumpadd),
    .Output_Branch(arithmetic_logic_unit_1_output_branch),
    .Output_StoreAddress(arithmetic_logic_unit_1_output_storeaddress),
    .Output_StoreData(arithmetic_logic_unit_1_output_storedata),
    .Output_LoadAddress(arithmetic_logic_unit_1_output_loadaddress));
  Multiplexer #(.width(24), .enable("false")) multiplexer_5 (
    .in0(arithmetic_logic_unit_1_output_storeaddress), .in1(arithmetic_logic_unit_1_output_loadaddress),
    .out(multiplexer_5_out), .sel(control_unit_1_dmemselectforload));
  RAM #(.addrWidth(24), .dataWidth(32), .bus("separate"), .Select("low")) ram_1 (
    .addr(multiplexer_5_out), .din(arithmetic_logic_unit_1_output_storedata), .data(ram_1_data),
    .sel(control_unit_1_dmemen), .clk(clock_1_out));  // open: str, ld, clr

  // Notes on the sheet:
  //   PROGRAM COUNTER
  //   INSTRUCTION MEMORY
  //   contents of rom_1 (hex, n*v repeats v):
  //   500293 500213 428133
endmodule

// Control Unit
module control_unit (
  input  [31:0] in_1,
  output RegWEn,
  output Bsel,
  output DMemEn,
  output branchInstruction,
  output DMemSelectForLoad
);

  wire comparator_1_eq, comparator_3_eq, comparator_4_eq, or_3_out;

  Comparator #(.width(7)) comparator_1 (.a(7'b0110011), .b(in_1[6:0]), .eq(comparator_1_eq));  // open: gt, lt
  Comparator #(.width(7)) comparator_2 (.a(7'b1100011), .b(in_1[6:0]), .eq(branchInstruction));  // open: gt, lt
  Comparator #(.width(7)) comparator_3 (.a(7'b0010011), .b(in_1[6:0]), .eq(comparator_3_eq));  // open: gt, lt
  Comparator #(.width(7)) comparator_4 (.a(7'b0100011), .b(in_1[6:0]), .eq(comparator_4_eq));  // open: gt, lt
  Comparator #(.width(7)) comparator_5 (.a(7'b0000011), .b(in_1[6:0]), .eq(DMemSelectForLoad));  // open: gt, lt
  or or_1 (RegWEn, comparator_1_eq, DMemSelectForLoad, comparator_3_eq);
  or or_2 (Bsel, comparator_3_eq, DMemSelectForLoad);
  or or_3 (or_3_out, comparator_4_eq, DMemSelectForLoad);
  not not_1 (DMemEn, or_3_out);
endmodule
